# Fritzing sketch rainbow (saved by Fritzing 1.0.2b)
breadboards: 1

parts:
  A1 = Esp32-c3 super mini
  C1 = Electrolytic Capacitor [capacitance=1mF voltage=35V package="100 mil [THT, electrolytic]"]
  R1 = Resistor [tolerance=±5% power=0.25W resistance=330 package=THT]
  A2 = usbc to 12V module
  Part1 = ws2812b [package="smd 2812b"]
  R2 = Photocell (LDR) [power=0.25W dark_resistance_@0.01lx=300kΩ light_resistance_@100lx=400Ω luminance=10lx package=THT]
  R3 = Resistor [tolerance=±5% power=0.25W resistance=10k package=THT]

nets:
  N1: A1.Pin_9, R2.pin_1, R3.Pin_0
  N2: A1.Pin_13, R1.Pin_0
  N3: A1.Pin_14, R2.pin_0
  N4: A1.Pin_15, C1.-, A2.Pin_1, A2.Pin_2, Part1.VSS, R3.Pin_1
  N5: A1.Pin_16, C1.+, A2.Pin_3, A2.Pin_4, Part1.VDD
  N6: R1.Pin_1, Part1.DIN

custom parts:
  Esp32-c3 super mini: ESP32-C3 Development Board ESP32 SuperMini Development Board ESP32 Development Board WiFi Bluetooth.
  usbc to 12V module: usbc to 12V module.
